# Fritzing sketch breadboard circuit diagrams DRV8825 PB6600 L298N Trinket Pro (saved by Fritzing 1.0.4)
breadboards: 3

parts:
  Part1 = Adafruit Pro Trinket 5V 16MHz [part_number="Adafruit #2000"]
  M1 = Stepper Motor - Bipolar
  S2 = Pushbutton [package="[THT]"]
  U1 = LIPO-1000mAh [package=lipo-1000]
  U2 = LIPO-1000mAh [package=lipo-1000]
  U3 = LIPO-1000mAh [package=lipo-1000]
  U4 = LIPO-1000mAh [package=lipo-1000]
  IC1 = Voltage Regulator [package=to220-igo]
  S3 = Pushbutton [package="[THT]"]
  L298N1 = L298N DC motor driver
  A1 = TB6600 NEMA-17-23 STEPPER MOTOR DRIVER [package=THT]
  Part2 = Adafruit Pro Trinket 5V 16MHz [part_number="Adafruit #2000"]
  M2 = Stepper Motor - Bipolar  # not connected
  S4 = Pushbutton [package="[THT]"]
  S5 = Pushbutton [package="[THT]"]
  U5 = LIPO-1000mAh [package=lipo-1000]
  U6 = LIPO-1000mAh [package=lipo-1000]
  U7 = LIPO-1000mAh [package=lipo-1000]
  U8 = LIPO-1000mAh [package=lipo-1000]
  IC2 = Voltage Regulator [package=to220-igo]
  R2 = Resistor [tolerance=±5% power=0.25W resistance=10k package=THT]
  Part3 = Adafruit Pro Trinket 5V 16MHz [part_number="Adafruit #2000"]
  M3 = Stepper Motor - Bipolar
  S6 = Pushbutton [package="[THT]"]
  S7 = Pushbutton [package="[THT]"]
  U9 = LIPO-1000mAh [package=lipo-1000]
  U10 = LIPO-1000mAh [package=lipo-1000]
  U11 = LIPO-1000mAh [package=lipo-1000]
  U12 = LIPO-1000mAh [package=lipo-1000]
  IC3 = Voltage Regulator [package=to220-igo]
  DRV_2 = DRV 8825 Stepper Motor Carrier, High Current [part_number="DRV 8825"]  # not connected

nets:
  GND: Part1.GND, Part1.D9, Part1.D10, S2.Pin_3, S2.Pin_4, U4.-, IC1.GND, S3.Pin_3, S3.Pin_4, A1.pin_5, A1.pin_7, A1.pin_8, A1.pin_9, A1.pin_11
  N1: Part1.VBUS, IC1.OUT
  N2: Part1.A2, A1.pin_10
  N3: Part1.A3, A1.pin_12
  N4: M1.A, A1.pin_1
  N5: M1.C, A1.pin_2
  N6: M1.B, A1.pin_3
  N7: M1.D, A1.pin_4
  N8: S2.Pin_1, S2.Pin_2
  N9: U1.+, IC1.IN, A1.pin_6
  N10: U1.-, U2.+
  N11: U2.-, U3.+
  N12: U3.-, U4.+
  N13: S3.Pin_1, S3.Pin_2
  N14: L298N1.OUT1, M3.D
  N15: L298N1.OUT2, M3.B
  N16: L298N1.OUT3, M3.C
  N17: L298N1.OUT4, M3.A
  N18: L298N1.12V, U9.+, IC3.IN
  GND_2: L298N1.GND, Part3.GND, Part3.D9, Part3.D10, S6.Pin_3, S6.Pin_4, S7.Pin_3, S7.Pin_4, U12.-, IC3.GND
  N19: L298N1.5V, Part3.VBUS, IC3.OUT
  N20: L298N1.IN1, Part3.A3
  N21: L298N1.IN2, Part3.A2
  N22: L298N1.IN3, Part3.A1
  N23: L298N1.IN4, Part3.D13
  GND_3: Part2.GND, Part2.D9, Part2.D10, S4.Pin_3, S4.Pin_4, S5.Pin_3, S5.Pin_4, U8.-, IC2.GND
  N24: Part2.VBUS, IC2.OUT, R2.Pin_0
  N25: S4.Pin_1, S4.Pin_2
  N26: S5.Pin_1, S5.Pin_2
  N27: U5.+, IC2.IN
  N28: U5.-, U6.+
  N29: U6.-, U7.+
  N30: U7.-, U8.+
  N31: S6.Pin_1, S6.Pin_2
  N32: S7.Pin_1, S7.Pin_2
  N33: U9.-, U10.+
  N34: U10.-, U11.+
  N35: U11.-, U12.+

notes:
  Warning: remove 5V jumper, and supply 5V as shown here if Vmotor > 12V

custom parts:
  Adafruit Pro Trinket 5V 16MHz: Trinket's got a big sister in town - the Pro Trinket 5V! Pro Trinket combines everything you love about Trinket with the familiarity of the common core Arduino chip, the ATmega328. It's like an Arduino Pro Mini with more pins and USB tossed in, so delicious. Trinket's a year old now, and while its been great to see tons of tiny projects, sometimes you just need more pins, more FLASH, and more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
  Pushbutton: A generic pushbutton.
  L298N DC motor driver: 2x DC motor driver with 78M05 positive voltage regulator (7..35 V) L298N: max 46 V, 2 A Set 5 V Enable jumper to enable 5 V regultor (needed for the L298N) and +5 V output at screw terminal or supply external +5 V at screw terminal Set ENA and/or ENB to +5 V to enable motor permanently or supply ENA and/or ENB with PWM signal IN1 and IN2 set rotation directory for motor A (OUT1/OUT2) IN2 and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
  TB6600 NEMA-17-23 STEPPER MOTOR DRIVER: cheap Nema-17-23 steppermotor driver board
